// Logisim project 7seg.circ as structural Verilog
module _7seg (
  input  D,
  input  C,
  input  B,
  input  A,
  output a_2,
  output b_2,
  output c_2,
  output d_2,
  output e,
  output f,
  output g
);

  wire and_1_out, and_2_out, and_3_out, and_4_out, and_5_out, and_6_out, and_7_out, and_8_out, and_9_out,
       and_10_out, and_11_out, and_12_out, and_13_out, and_14_out, and_15_out, not_1_out, not_2_out,
       not_3_out, not_4_out, not_5_out, not_6_out, not_7_out, not_8_out, not_9_out, not_10_out, not_11_out,
       not_12_out, not_13_out, not_14_out, not_15_out, not_16_out, not_17_out, not_18_out, not_19_out,
       not_20_out, not_21_out, or_1_out, or_2_out, or_3_out, or_4_out, or_5_out, or_6_out, or_7_out,
       or_10_out, or_11_out, or_12_out, or_13_out, or_15_out, or_16_out, undriven;

  or or_1 (or_1_out, D, C);
  or or_2 (or_2_out, B, not_1_out);
  not not_1 (not_1_out, A);
  not not_2 (not_2_out, C);
  or or_3 (or_3_out, not_2_out, B);
  not not_3 (not_3_out, C);
  not not_4 (not_4_out, B);
  and and_1 (and_1_out, not_4_out, not_5_out);
  not not_5 (not_5_out, A);
  not not_6 (not_6_out, B);
  or or_4 (or_4_out, not_6_out, A);
  not not_7 (not_7_out, C);
  not not_8 (not_8_out, A);
  not not_9 (not_9_out, C);
  not not_10 (not_10_out, A);
  and and_2 (and_2_out, C, not_11_out);
  not not_11 (not_11_out, B);
  not not_12 (not_12_out, C);
  and and_3 (and_3_out, not_12_out, not_13_out);
  not not_13 (not_13_out, A);
  and and_4 (and_4_out, B, not_14_out);
  not not_14 (not_14_out, A);
  not not_15 (not_15_out, B);
  and and_5 (and_5_out, not_15_out, not_16_out);
  not not_16 (not_16_out, A);
  and and_6 (and_6_out, C, not_17_out);
  not not_17 (not_17_out, B);
  and and_7 (and_7_out, C, not_18_out);
  not not_18 (not_18_out, A);
  not not_19 (not_19_out, C);
  and and_8 (and_8_out, not_19_out, B);
  and and_9 (and_9_out, C, not_20_out);
  not not_20 (not_20_out, B);
  and and_10 (and_10_out, C, not_21_out);
  not not_21 (not_21_out, A);
  or or_5 (or_5_out, or_1_out, or_2_out);
  or or_6 (or_6_out, or_3_out, A);
  or or_7 (or_7_out, not_3_out, and_1_out);
  and and_11 (and_11_out, B, A);
  or or_8 (c_2, or_4_out, C);
  and and_12 (and_12_out, not_7_out, not_8_out);
  and and_13 (and_13_out, not_9_out, B);
  and and_14 (and_14_out, B, not_10_out);
  and and_15 (and_15_out, and_2_out, A);
  or or_9 (e, and_3_out, and_4_out);
  or or_10 (or_10_out, and_5_out, and_6_out);
  or or_11 (or_11_out, and_7_out, D);
  or or_12 (or_12_out, and_8_out, and_9_out);
  or or_13 (or_13_out, and_10_out, D);
  and and_16 (a_2, or_5_out, or_6_out);
  or or_14 (b_2, or_7_out, and_11_out);
  or or_15 (or_15_out, and_12_out, and_13_out);
  or or_16 (or_16_out, and_14_out, and_15_out);
  or or_17 (f, or_10_out, or_11_out);
  or or_18 (g, or_12_out, or_13_out);
  or or_19 (d_2, or_15_out, or_16_out);
  _7_Segment_Display u_7_segment_display_1 (.g(g), .f(f), .a(a_2), .b(b_2), .e(e), .d(d_2), .c(c_2), .dp(undriven));
endmodule
